# Fritzing sketch basic_ssd1306 (saved by Fritzing 0.9.6b)
circuit board: 8.46667cm x 5.64444cm
breadboards: 1

parts:
  Pico = Raspberry Pi Pico
  SSD1306_I2C = OLED 128x64 I2C Monochrome Display

nets:
  N1: Pico.pin_3, Pico.pin_38, Pico.pin_42, SSD1306_I2C.GND
  N2: Pico.pin_9, SSD1306_I2C.SDA
  N3: Pico.pin_36, SSD1306_I2C.VDD

custom parts:
  Raspberry Pi Pico: Raspberry Pi Pico. Based around the RP2040 microcontroller the Pico is a low cost microcontroller device bringing Raspberry Pi quality, cost, and easy of use to the microcontroller space. Jan 2021, Split part in to two versions: tht (this one) and SMD. This one will drill holes for a .1 in header in pcb to allow plugging in the module as well as providing pads to solder the module to the top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
